// Digital circuit ALUCPU.dig as structural Verilog
module ALUCPU (
  input  A0,
  input  B0,
  input  A1,
  input  B1,
  input  A2,
  input  B2,
  input  A3,
  input  B3,
  input  A4,
  input  B4,
  input  A5,
  input  B5,
  input  A6,
  input  B6,
  input  A7,
  input  B7,
  input  C0,
  input  C1,
  input  C2,
  input  Nlb,
  input  Clk,
  output out_20,
  output eq,
  output plus,
  output S0,
  output S1,
  output S2,
  output S3,
  output S4,
  output S5,
  output S6,
  output S7
);

  wire adder_1_ovf, adder_1_s0, adder_1_s1, adder_1_s2, adder_1_s3, adder_1_s4, adder_1_s5, adder_1_s6,
       adder_1_s7, bitshifter_1_s0, bitshifter_1_s1, bitshifter_1_s2, bitshifter_1_s3, bitshifter_1_s4,
       bitshifter_1_s5, bitshifter_1_s6, bitshifter_1_s7, comparador8bit_1_a_eq_b, comparador8bit_1_a_gt_b,
       comparador8bit_1_a_lt_b, driver_1_out, driver_2_out, driver_3_out, driver_4_out, driver_5_out,
       driver_6_out, driver_7_out, driver_8_out, driver_9_out, driver_10_out, driver_11_out, driver_12_out,
       driver_13_out, driver_14_out, driver_15_out, driver_16_out, driver_17_out, driver_18_out,
       driver_19_out, driver_20_out, driver_21_out, driver_22_out, driver_23_out, driver_24_out,
       driver_25_out, driver_26_out, driver_27_out, driver_28_out, driver_29_out, driver_30_out,
       driver_31_out, driver_32_out, driver_34_out, driver_35_out, driver_36_out, driver_37_out,
       driver_38_out, multiplicador_1_s0, multiplicador_1_s1, multiplicador_1_s2, multiplicador_1_s3,
       multiplicador_1_s4, multiplicador_1_s5, multiplicador_1_s6, multiplicador_1_s7, not_1_out,
       pulldown_2_out, pulldown_3_out, pulldown_4_out, pulldown_5_out, pulldown_6_out, pulldown_7_out,
       pulldown_8_out, pulldown_9_out, pulldown_13_out, seletor_1_s0, seletor_1_s1, seletor_1_s2,
       seletor_1_s3, seletor_1_s4, seletor_1_s5, seletor_1_s6, subtractor8_1_d0, subtractor8_1_d1,
       subtractor8_1_d2, subtractor8_1_d3, subtractor8_1_d4, subtractor8_1_d5, subtractor8_1_d6,
       subtractor8_1_d7, subtractor8_1_neg;

  Seven_Seg_Hex seven_seg_hex_1 (.d({S3, S2, S1, S0}), .dp(1'b0));
  not not_1 (not_1_out, Nlb);
  PullDown pulldown_1 (.out(plus));
  PullDown pulldown_2 (.out(pulldown_2_out));
  PullDown pulldown_3 (.out(pulldown_3_out));
  PullDown pulldown_4 (.out(pulldown_4_out));
  PullDown pulldown_5 (.out(pulldown_5_out));
  PullDown pulldown_6 (.out(pulldown_6_out));
  PullDown pulldown_7 (.out(pulldown_7_out));
  PullDown pulldown_8 (.out(pulldown_8_out));
  PullDown pulldown_9 (.out(pulldown_9_out));
  Seven_Seg_Hex seven_seg_hex_2 (.d({S7, S6, S5, S4}), .dp(1'b0));
  Register register_1 (
    .D0(pulldown_9_out), .R(1'b1), .C(Clk), .W(not_1_out), .Cir(1'b0), .D1(pulldown_8_out),
    .D2(pulldown_7_out), .D3(pulldown_6_out), .D4(pulldown_5_out), .D5(pulldown_4_out), .D6(pulldown_3_out),
    .D7(pulldown_2_out), .Q0(S0), .Q1(S1), .Q2(S2), .Q3(S3), .Q4(S4), .Q5(S5), .Q6(S6), .Q7(S7));
  PullDown pulldown_10 (.out(plus));
  PullDown pulldown_11 (.out(eq));
  PullDown pulldown_12 (.out(out_20));
  DiodeForward diodeforward_1 (.in(driver_32_out), .out(pulldown_2_out));
  DiodeForward diodeforward_2 (.in(driver_28_out), .out(pulldown_3_out));
  DiodeForward diodeforward_3 (.in(driver_24_out), .out(pulldown_4_out));
  DiodeForward diodeforward_4 (.in(driver_20_out), .out(pulldown_5_out));
  DiodeForward diodeforward_5 (.in(driver_16_out), .out(pulldown_6_out));
  DiodeForward diodeforward_6 (.in(driver_11_out), .out(pulldown_7_out));
  DiodeForward diodeforward_7 (.in(driver_6_out), .out(pulldown_8_out));
  assign driver_1_out = seletor_1_s3 ? multiplicador_1_s0 : 1'bz;  // Driver driver_1
  DiodeForward diodeforward_8 (.in(driver_1_out), .out(pulldown_9_out));
  DiodeForward diodeforward_9 (.in(driver_34_out), .out(pulldown_2_out));
  DiodeForward diodeforward_10 (.in(driver_29_out), .out(pulldown_3_out));
  DiodeForward diodeforward_11 (.in(driver_25_out), .out(pulldown_4_out));
  DiodeForward diodeforward_12 (.in(driver_21_out), .out(pulldown_5_out));
  DiodeForward diodeforward_13 (.in(driver_17_out), .out(pulldown_6_out));
  DiodeForward diodeforward_14 (.in(driver_12_out), .out(pulldown_7_out));
  DiodeForward diodeforward_15 (.in(driver_7_out), .out(pulldown_8_out));
  assign driver_2_out = pulldown_13_out ? bitshifter_1_s0 : 1'bz;  // Driver driver_2
  DiodeForward diodeforward_16 (.in(driver_2_out), .out(pulldown_9_out));
  DiodeForward diodeforward_17 (.in(driver_13_out), .out(plus));
  DiodeForward diodeforward_18 (.in(driver_8_out), .out(eq));
  assign driver_3_out = seletor_1_s2 ? comparador8bit_1_a_lt_b : 1'bz;  // Driver driver_3
  DiodeForward diodeforward_19 (.in(driver_3_out), .out(out_20));
  DiodeForward diodeforward_20 (.in(driver_37_out), .out(out_20));
  DiodeForward diodeforward_21 (.in(driver_35_out), .out(pulldown_2_out));
  DiodeForward diodeforward_22 (.in(driver_30_out), .out(pulldown_3_out));
  DiodeForward diodeforward_23 (.in(driver_26_out), .out(pulldown_4_out));
  DiodeForward diodeforward_24 (.in(driver_22_out), .out(pulldown_5_out));
  DiodeForward diodeforward_25 (.in(driver_18_out), .out(pulldown_6_out));
  DiodeForward diodeforward_26 (.in(driver_14_out), .out(pulldown_7_out));
  DiodeForward diodeforward_27 (.in(driver_9_out), .out(pulldown_8_out));
  assign driver_4_out = seletor_1_s1 ? subtractor8_1_d0 : 1'bz;  // Driver driver_4
  DiodeForward diodeforward_28 (.in(driver_4_out), .out(pulldown_9_out));
  DiodeForward diodeforward_29 (.in(driver_38_out), .out(plus));
  DiodeForward diodeforward_30 (.in(driver_36_out), .out(pulldown_2_out));
  DiodeForward diodeforward_31 (.in(driver_31_out), .out(pulldown_3_out));
  DiodeForward diodeforward_32 (.in(driver_27_out), .out(pulldown_4_out));
  DiodeForward diodeforward_33 (.in(driver_23_out), .out(pulldown_5_out));
  DiodeForward diodeforward_34 (.in(driver_19_out), .out(pulldown_6_out));
  DiodeForward diodeforward_35 (.in(driver_15_out), .out(pulldown_7_out));
  DiodeForward diodeforward_36 (.in(driver_10_out), .out(pulldown_8_out));
  assign driver_5_out = seletor_1_s0 ? adder_1_s0 : 1'bz;  // Driver driver_5
  DiodeForward diodeforward_37 (.in(driver_5_out), .out(pulldown_9_out));
  assign driver_6_out = seletor_1_s3 ? multiplicador_1_s1 : 1'bz;  // Driver driver_6
  assign driver_7_out = pulldown_13_out ? bitshifter_1_s1 : 1'bz;  // Driver driver_7
  assign driver_8_out = seletor_1_s2 ? comparador8bit_1_a_eq_b : 1'bz;  // Driver driver_8
  assign driver_9_out = seletor_1_s1 ? subtractor8_1_d1 : 1'bz;  // Driver driver_9
  assign driver_10_out = seletor_1_s0 ? adder_1_s1 : 1'bz;  // Driver driver_10
  assign driver_11_out = seletor_1_s3 ? multiplicador_1_s2 : 1'bz;  // Driver driver_11
  assign driver_12_out = pulldown_13_out ? bitshifter_1_s2 : 1'bz;  // Driver driver_12
  assign driver_13_out = seletor_1_s2 ? comparador8bit_1_a_gt_b : 1'bz;  // Driver driver_13
  assign driver_14_out = seletor_1_s1 ? subtractor8_1_d2 : 1'bz;  // Driver driver_14
  assign driver_15_out = seletor_1_s0 ? adder_1_s2 : 1'bz;  // Driver driver_15
  assign driver_16_out = seletor_1_s3 ? multiplicador_1_s3 : 1'bz;  // Driver driver_16
  assign driver_17_out = pulldown_13_out ? bitshifter_1_s3 : 1'bz;  // Driver driver_17
  assign driver_18_out = seletor_1_s1 ? subtractor8_1_d3 : 1'bz;  // Driver driver_18
  assign driver_19_out = seletor_1_s0 ? adder_1_s3 : 1'bz;  // Driver driver_19
  assign driver_20_out = seletor_1_s3 ? multiplicador_1_s4 : 1'bz;  // Driver driver_20
  assign driver_21_out = pulldown_13_out ? bitshifter_1_s4 : 1'bz;  // Driver driver_21
  assign driver_22_out = seletor_1_s1 ? subtractor8_1_d4 : 1'bz;  // Driver driver_22
  assign driver_23_out = seletor_1_s0 ? adder_1_s4 : 1'bz;  // Driver driver_23
  assign driver_24_out = seletor_1_s3 ? multiplicador_1_s5 : 1'bz;  // Driver driver_24
  assign driver_25_out = pulldown_13_out ? bitshifter_1_s5 : 1'bz;  // Driver driver_25
  assign driver_26_out = seletor_1_s1 ? subtractor8_1_d5 : 1'bz;  // Driver driver_26
  assign driver_27_out = seletor_1_s0 ? adder_1_s5 : 1'bz;  // Driver driver_27
  assign driver_28_out = seletor_1_s3 ? multiplicador_1_s6 : 1'bz;  // Driver driver_28
  assign driver_29_out = pulldown_13_out ? bitshifter_1_s6 : 1'bz;  // Driver driver_29
  assign driver_30_out = seletor_1_s1 ? subtractor8_1_d6 : 1'bz;  // Driver driver_30
  assign driver_31_out = seletor_1_s0 ? adder_1_s6 : 1'bz;  // Driver driver_31
  assign driver_32_out = seletor_1_s3 ? multiplicador_1_s7 : 1'bz;  // Driver driver_32
  assign driver_32_out = seletor_1_s3 ? multiplicador_1_s7 : 1'bz;  // Driver driver_33
  assign driver_34_out = pulldown_13_out ? bitshifter_1_s7 : 1'bz;  // Driver driver_34
  comparador8bit comparador8bit_1 (
    .A({A7, A6, A5, A4, A3, A2, A1, A0}), .B({B7, B6, B5, B4, B3, B2, B1, B0}),
    .A_lt_B(comparador8bit_1_a_lt_b), .A_eq_B(comparador8bit_1_a_eq_b), .A_gt_B(comparador8bit_1_a_gt_b));
  assign driver_35_out = seletor_1_s1 ? subtractor8_1_d7 : 1'bz;  // Driver driver_35
  assign driver_36_out = seletor_1_s0 ? adder_1_s7 : 1'bz;  // Driver driver_36
  assign driver_37_out = seletor_1_s1 ? subtractor8_1_neg : 1'bz;  // Driver driver_37
  assign driver_38_out = seletor_1_s0 ? adder_1_ovf : 1'bz;  // Driver driver_38
  multiplicador multiplicador_1 (
    .A0(A0), .A1(A1), .A2(A2), .A3(A3), .B0(B0), .B1(B1), .B2(B2), .B3(B3), .S0(multiplicador_1_s0),
    .S1(multiplicador_1_s1), .S2(multiplicador_1_s2), .S3(multiplicador_1_s3), .S4(multiplicador_1_s4),
    .S5(multiplicador_1_s5), .S6(multiplicador_1_s6), .S7(multiplicador_1_s7));
  BitShifter bitshifter_1 (
    .I0(A0), .Shift(seletor_1_s4), .I1(A1), .I2(A2), .I3(A3), .I4(A4), .I5(A5), .I6(A6), .I7(A7),
    .S0(bitshifter_1_s0), .S1(bitshifter_1_s1), .S2(bitshifter_1_s2), .S3(bitshifter_1_s3),
    .S4(bitshifter_1_s4), .S5(bitshifter_1_s5), .S6(bitshifter_1_s6), .S7(bitshifter_1_s7));
  Subtractor8 subtractor8_1 (
    .A0(A0), .B0(B0), .A1(A1), .B1(B1), .A2(A2), .B2(B2), .A3(A3), .B3(B3), .A4(A4), .B4(B4), .A5(A5),
    .B5(B5), .A6(A6), .B6(B6), .A7(A7), .B7(B7), .D0(subtractor8_1_d0), .D1(subtractor8_1_d1),
    .D2(subtractor8_1_d2), .D3(subtractor8_1_d3), .D4(subtractor8_1_d4), .D5(subtractor8_1_d5),
    .D6(subtractor8_1_d6), .D7(subtractor8_1_d7), .Neg(subtractor8_1_neg));
  Adder adder_1 (
    .A0(A0), .B0(B0), .A1(A1), .B1(B1), .A2(A2), .B2(B2), .A3(A3), .B3(B3), .A4(A4), .B4(B4), .A5(A5),
    .B5(B5), .A6(A6), .B6(B6), .A7(A7), .B7(B7), .S0(adder_1_s0), .S1(adder_1_s1), .S2(adder_1_s2),
    .S3(adder_1_s3), .S4(adder_1_s4), .S5(adder_1_s5), .S6(adder_1_s6), .S7(adder_1_s7), .OVF(adder_1_ovf));
  PullDown pulldown_13 (.out(pulldown_13_out));
  DiodeForward diodeforward_38 (.in(seletor_1_s5), .out(pulldown_13_out));
  DiodeForward diodeforward_39 (.in(seletor_1_s4), .out(pulldown_13_out));
  Seletor seletor_1 (
    .A(C0), .B(C1), .C(C2), .D(seletor_1_s6), .S0(seletor_1_s0), .S1(seletor_1_s1), .S2(seletor_1_s2),
    .S3(seletor_1_s3), .S4(seletor_1_s4), .S5(seletor_1_s5), .S6(seletor_1_s6), .S7(seletor_1_s6),
    .S8(seletor_1_s6));
  // also tied to GND on the sheet: seletor_1_s6

  // Notes on the sheet:
  //   C0: 000 - Sum
  //   001 - Sub
  //   010 - Comp
  //   011 - Multi
  //   100 - ShiftR
  //   101 - ShiftL
  //   C1: 000 - Sum
  //   001 - Sub
  //   010 - Comp
  //   011 - Multi
  //   100 - ShiftR
  //   101 - ShiftL
  //   C2: 000 - Sum
  //   001 - Sub
  //   010 - Comp
  //   011 - Multi
  //   100 - ShiftR
  //   101 - ShiftL
  //   000 - Sum
  //   001 - Sub
  //   010 - Comp
  //   011 - Multi
  //   100 - ShiftR
  //   101 - ShiftL
endmodule
