// Digital circuit CPU.dig as structural Verilog
module CPU (
  input  Op0,
  input  Op1,
  input  Op2
);

  wire acumulador_1_s0, acumulador_1_s1, acumulador_1_s2, acumulador_1_s3, acumulador_1_s4, acumulador_1_s5,
       acumulador_1_s6, acumulador_1_s7, Ad, alu_1_eq, alu_1_out_20, alu_1_plus, alu_1_s0, alu_1_s1,
       alu_1_s2, alu_1_s3, alu_1_s4, alu_1_s5, alu_1_s6, alu_1_s7, Clk, Clr, Cp, Ea, Ep,
       instruction_register_1_c0, memory_address_register_1_s0, memory_address_register_1_s1,
       memory_address_register_1_s2, memory_address_register_1_s3, memory_address_register_1_s4,
       memory_address_register_1_s5, memory_address_register_1_s6, memory_address_register_1_s7, NCE, NEi,
       NLa, NLb, NLi, NLm, NLo, register_b_1_s0, register_b_1_s1, register_b_1_s2, register_b_1_s3,
       register_b_1_s4, register_b_1_s5, register_b_1_s6, register_b_1_s7, ring_counter_1_p2,
       ring_counter_1_p3, ring_counter_1_p4;
  wire [3:0] register_out_1_s3, register_out_1_s7;

  DiodeForward diodeforward_1 (.in(ring_counter_1_p4), .out(NLa));
  PullDown pulldown_1 (.out(NLa));
  PullDown pulldown_2 (.out(Ea));
  PullDown pulldown_3 (.out(Clk));
  DiodeForward diodeforward_2 (.in(ring_counter_1_p3), .out(NLa));
  DiodeForward diodeforward_3 (.in(ring_counter_1_p2), .out(NLa));
  DiodeForward diodeforward_4 (.in(ring_counter_1_p4), .out(NLb));
  PullDown pulldown_4 (.out(NLb));
  PullDown pulldown_5 (.out(Clk));
  DiodeForward diodeforward_5 (.in(ring_counter_1_p3), .out(NLb));
  DiodeForward diodeforward_6 (.in(ring_counter_1_p2), .out(NLb));
  PullDown pulldown_6 (.out(Clk));
  DiodeForward diodeforward_7 (.in(ring_counter_1_p4), .out(NLo));
  DiodeForward diodeforward_8 (.in(ring_counter_1_p3), .out(NLo));
  DiodeForward diodeforward_9 (.in(ring_counter_1_p2), .out(NLo));
  PullDown pulldown_7 (.out(NLo));
  LED led (.in(alu_1_out_20));
  LED eq (.in(alu_1_eq));
  LED plus (.in(alu_1_plus));
  ALU alu_1 (
    .A0(acumulador_1_s0), .B0(register_b_1_s0), .A1(acumulador_1_s1), .B1(register_b_1_s1),
    .A2(acumulador_1_s2), .B2(register_b_1_s2), .A3(acumulador_1_s3), .B3(register_b_1_s3),
    .A4(acumulador_1_s4), .B4(register_b_1_s4), .A5(acumulador_1_s5), .B5(register_b_1_s5),
    .A6(acumulador_1_s6), .B6(register_b_1_s6), .A7(acumulador_1_s7), .B7(register_b_1_s7), .C0(Op0),
    .C1(Op1), .C2(Op2), .Nlb(Ea), .out_20(alu_1_out_20), .eq(alu_1_eq), .plus(alu_1_plus), .S0(alu_1_s0),
    .S1(alu_1_s1), .S2(alu_1_s2), .S3(alu_1_s3), .S4(alu_1_s4), .S5(alu_1_s5), .S6(alu_1_s6), .S7(alu_1_s7));  // open: Clk
  Seven_Seg_Hex seven_seg_hex_1 (.d(register_out_1_s3), .dp(1'b0));
  Seven_Seg_Hex seven_seg_hex_2 (.d(register_out_1_s7), .dp(1'b0));
  Acumulador acumulador_1 (
    .NLa(NLa), .Ea(Ea), .Clk(Clk), .I0(alu_1_s0), .I1(alu_1_s1), .I2(alu_1_s2), .I3(alu_1_s3), .I4(alu_1_s4),
    .I5(alu_1_s5), .I6(alu_1_s6), .I7(alu_1_s7), .S0(acumulador_1_s0), .S1(acumulador_1_s1),
    .S2(acumulador_1_s2), .S3(acumulador_1_s3), .S4(acumulador_1_s4), .S5(acumulador_1_s5),
    .S6(acumulador_1_s6), .S7(acumulador_1_s7));
  Button u_Clr (.out(Clr));
  Button u_Clk (.out(Clk));
  Register_out register_out_1 (
    .NLo(NLo), .Clk(Clk), .I0(alu_1_s0), .I1(alu_1_s1), .I2(alu_1_s2), .I3(alu_1_s3), .I4(alu_1_s4),
    .I5(alu_1_s5), .I6(alu_1_s6), .I7(alu_1_s7), .S0(register_out_1_s3[0]), .S1(register_out_1_s3[1]),
    .S2(register_out_1_s3[2]), .S3(register_out_1_s3[3]), .S4(register_out_1_s7[0]),
    .S5(register_out_1_s7[1]), .S6(register_out_1_s7[2]), .S7(register_out_1_s7[3]));
  Register_B register_b_1 (
    .NLb(NLb), .Clk(Clk), .I0(alu_1_s0), .I1(alu_1_s1), .I2(alu_1_s2), .I3(alu_1_s3), .I4(alu_1_s4),
    .I5(alu_1_s5), .I6(alu_1_s6), .I7(alu_1_s7), .S0(register_b_1_s0), .S1(register_b_1_s1),
    .S2(register_b_1_s2), .S3(register_b_1_s3), .S4(register_b_1_s4), .S5(register_b_1_s5),
    .S6(register_b_1_s6), .S7(register_b_1_s7));
  Memory_Address_Register memory_address_register_1 (
    .NLm(NLm), .Clk(Clk), .I0(alu_1_s0), .I1(alu_1_s1), .I2(alu_1_s2), .I3(alu_1_s3), .I4(alu_1_s4),
    .I5(alu_1_s5), .I6(alu_1_s6), .I7(alu_1_s7), .S0(memory_address_register_1_s0),
    .S1(memory_address_register_1_s1), .S2(memory_address_register_1_s2), .S3(memory_address_register_1_s3),
    .S4(memory_address_register_1_s4), .S5(memory_address_register_1_s5), .S6(memory_address_register_1_s6),
    .S7(memory_address_register_1_s7));
  Program_Counter program_counter_1 (
    .Cp(Cp), .Ep(Ep), .NClr(Clr), .NClk(Clk), .S0(alu_1_s0), .S1(alu_1_s1), .S2(alu_1_s2), .S3(alu_1_s3));
  Instruction_Register instruction_register_1 (
    .NEi(NEi), .Clr(Clr), .Clk(Clk), .NLi(NLi), .I0(alu_1_s0), .I1(alu_1_s1), .I2(alu_1_s2), .I3(alu_1_s3),
    .I4(alu_1_s4), .I5(alu_1_s5), .I6(alu_1_s6), .I7(alu_1_s7), .C0(instruction_register_1_c0),
    .C1(instruction_register_1_c0), .C2(instruction_register_1_c0), .C3(instruction_register_1_c0),
    .Op0(alu_1_s4), .Op1(alu_1_s5), .Op2(alu_1_s6), .Op3(alu_1_s7));
  Random_Access_Memory random_access_memory_1 (
    .I0(memory_address_register_1_s0), .I1(memory_address_register_1_s1), .I2(memory_address_register_1_s2),
    .I3(memory_address_register_1_s3), .I4(memory_address_register_1_s4), .I5(memory_address_register_1_s5),
    .I6(memory_address_register_1_s6), .I7(memory_address_register_1_s7), .NCe(NCE), .Clr(Clr), .Clk(Clk),
    .A(memory_address_register_1_s0), .B(memory_address_register_1_s1), .C(memory_address_register_1_s2),
    .D(Ad), .S0(alu_1_s0), .S1(alu_1_s1), .S2(alu_1_s2), .S3(alu_1_s3), .S4(alu_1_s4), .S5(alu_1_s5),
    .S6(alu_1_s6), .S7(alu_1_s7));
  DiodeForward diodeforward_10 (.in(ring_counter_1_p3), .out(NEi));
  DiodeForward diodeforward_11 (.in(ring_counter_1_p2), .out(NEi));
  DiodeForward diodeforward_12 (.in(ring_counter_1_p4), .out(NLi));
  DiodeForward diodeforward_13 (.in(ring_counter_1_p4), .out(NEi));
  DiodeForward diodeforward_14 (.in(ring_counter_1_p3), .out(NLi));
  PullDown pulldown_8 (.out(NLi));
  PullDown pulldown_9 (.out(Clk));
  PullDown pulldown_10 (.out(Clr));
  PullDown pulldown_11 (.out(NEi));
  DiodeForward diodeforward_15 (.in(ring_counter_1_p4), .out(NCE));
  DiodeForward diodeforward_16 (.in(ring_counter_1_p4), .out(Ad));
  DiodeForward diodeforward_17 (.in(ring_counter_1_p3), .out(NCE));
  DiodeForward diodeforward_18 (.in(ring_counter_1_p3), .out(Ad));
  PullDown pulldown_12 (.out(NCE));
  PullDown pulldown_13 (.out(Clr));
  PullDown pulldown_14 (.out(Clk));
  PullDown pulldown_15 (.out(Ad));
  DiodeForward diodeforward_19 (.in(ring_counter_1_p2), .out(NLm));
  DiodeForward diodeforward_20 (.in(ring_counter_1_p3), .out(NLm));
  PullDown pulldown_16 (.out(Clk));
  PullDown pulldown_17 (.out(NLm));
  DiodeForward diodeforward_21 (.in(ring_counter_1_p3), .out(Cp));
  DiodeForward diodeforward_22 (.in(ring_counter_1_p4), .out(Ep));
  // Ring_Counter ring_counter_1: pin names not known; wires that end beside it: Ea, ring_counter_1_p2, ring_counter_1_p3, ring_counter_1_p4, Clr, Clk
  PullDown pulldown_18 (.out(Ep));
  PullDown pulldown_19 (.out(Clr));
  PullDown pulldown_20 (.out(Clk));
  PullDown pulldown_21 (.out(Cp));
  // also tied to GND on the sheet: instruction_register_1_c0

  // Other names for the same wires on the sheet: Eu = Ea

  // Notes on the sheet:
  //   FETCH:
  //   T2:
  //   Cp Ep NLm NCE Ad  NLi NEi NLa Ea  Eu NLb NLa
  //   1    0     1     1    1     1   1     1    0   0    1     1
  //   T1:
  //   Cp Ep NLm NCE Ad  NLi NEi NLa Ea  Eu NLb NLa
  //   1    0     1     1    1     1   1     1    0   0    1     1
  //   T0:
  //   Cp Ep NLm NCE Ad  NLi NEi NLa Ea  Eu NLb NLa
  //   0    1     0     1    1     1   1     1    0   0    1     1
endmodule
