// Digital circuit Random Access Memory.dig as structural Verilog
module Random_Access_Memory (
  input  I0,
  input  I1,
  input  I2,
  input  I3,
  input  I4,
  input  I5,
  input  I6,
  input  I7,
  input  NCe,
  input  Clr,
  input  Clk,
  input  A,
  input  B,
  input  C,
  input  Ad,
  output S0,
  output S1,
  output S2,
  output S3,
  output S4,
  output S5,
  output S6,
  output S7
);

  wire and_1_out, and_2_out, and_3_out, and_4_out, and_5_out, and_6_out, and_7_out, and_8_out, and_9_out,
       and_10_out, and_11_out, and_12_out, not_1_out, register_7_q3, selector_1_p1, selector_1_p2,
       selector_1_p3, selector_1_p4, selector_1_p5, selector_1_p6, selector_1_p7, selector_1_p8,
       selector_1_p9;

  Register register_1 (
    .D0(Clk), .R(and_1_out), .C(I0), .W(and_7_out), .Cir(Clr), .D1(I1), .D2(I2), .D3(I3), .D4(I4), .D5(I5),
    .D6(I6), .D7(I7), .Q0(S0), .Q1(S1), .Q2(S2), .Q3(S3), .Q4(S4), .Q5(S5), .Q6(S6), .Q7(S7));
  Register register_2 (
    .D0(Clk), .R(and_2_out), .C(I0), .W(and_8_out), .Cir(Clr), .D1(I1), .D2(I2), .D3(I3), .D4(I4), .D5(I5),
    .D6(I6), .D7(I7), .Q0(S0), .Q1(S1), .Q2(S2), .Q3(S3), .Q4(S4), .Q5(S5), .Q6(S6), .Q7(S7));
  Register register_3 (
    .D0(Clk), .R(and_3_out), .C(I0), .W(and_9_out), .Cir(Clr), .D1(I1), .D2(I2), .D3(I3), .D4(I4), .D5(I5),
    .D6(I6), .D7(I7), .Q0(S0), .Q1(S1), .Q2(S2), .Q3(S3), .Q4(S4), .Q5(S5), .Q6(S6), .Q7(S7));
  Register register_4 (
    .D0(Clk), .R(and_4_out), .C(I0), .W(and_10_out), .Cir(Clr), .D1(I1), .D2(I2), .D3(I3), .D4(I4), .D5(I5),
    .D6(I6), .D7(I7), .Q0(S0), .Q1(S1), .Q2(S2), .Q3(S3), .Q4(S4), .Q5(S5), .Q6(S6), .Q7(S7));
  Register register_5 (
    .D0(Clk), .R(and_5_out), .C(I0), .W(and_11_out), .Cir(Clr), .D1(I1), .D2(I2), .D3(I3), .D4(I4), .D5(I5),
    .D6(I6), .D7(I7), .Q0(S0), .Q1(S1), .Q2(S2), .Q3(S3), .Q4(S4), .Q5(S5), .Q6(S6), .Q7(S7));
  Register register_6 (
    .D0(Clk), .R(and_6_out), .C(I0), .W(and_12_out), .Cir(Clr), .D1(I1), .D2(I2), .D3(I3), .D4(I4), .D5(I5),
    .D6(I6), .D7(I7), .Q0(S0), .Q1(S1), .Q2(S2), .Q3(S3), .Q4(S4), .Q5(S5), .Q6(S6), .Q7(S7));
  and and_1 (and_1_out, not_1_out, selector_1_p1);
  and and_2 (and_2_out, not_1_out, selector_1_p2);
  and and_3 (and_3_out, not_1_out, selector_1_p3);
  and and_4 (and_4_out, not_1_out, selector_1_p4);
  and and_5 (and_5_out, not_1_out, selector_1_p5);
  and and_6 (and_6_out, not_1_out, selector_1_p6);
  and and_7 (and_7_out, not_1_out, selector_1_p1);
  and and_8 (and_8_out, not_1_out, selector_1_p2);
  and and_9 (and_9_out, not_1_out, selector_1_p3);
  and and_10 (and_10_out, not_1_out, selector_1_p4);
  and and_11 (and_11_out, not_1_out, selector_1_p5);
  and and_12 (and_12_out, not_1_out, selector_1_p6);
  not not_1 (not_1_out, NCe);
  // Selector selector_1: pin names not known; wires that end beside it: selector_1_p1, selector_1_p2, selector_1_p3, selector_1_p4, selector_1_p5, selector_1_p6, selector_1_p7, selector_1_p8, selector_1_p9
  Register register_7 (
    .D0(Clk), .R(not_1_out), .C(A), .W(Ad), .Cir(register_7_q3), .D1(B), .D2(C), .D3(register_7_q3),
    .D4(register_7_q3), .D5(register_7_q3), .D6(register_7_q3), .D7(register_7_q3), .Q0(selector_1_p9),
    .Q1(selector_1_p8), .Q2(selector_1_p7), .Q3(register_7_q3), .Q4(register_7_q3), .Q5(register_7_q3),
    .Q6(register_7_q3), .Q7(register_7_q3));
  // also tied to GND on the sheet: register_7_q3
endmodule
