// Digital circuit Ring-Counter.dig as structural Verilog
module Ring_Counter (
  input  Clk,
  input  Clr,
  output Q5,
  output Q4,
  output Q3,
  output Q2,
  output Q1,
  output Q0
);

  D_FF_AS d_ff_as_1 (.Set(Clr), .D(Q5), .C(Clk), .Clr(1'b0), .Q(Q0));  // open: nQ
  D_FF_AS d_ff_as_2 (.Set(1'b0), .D(Q0), .C(Clk), .Clr(Clr), .Q(Q1));  // open: nQ
  D_FF_AS d_ff_as_3 (.Set(1'b0), .D(Q1), .C(Clk), .Clr(Clr), .Q(Q2));  // open: nQ
  D_FF_AS d_ff_as_4 (.Set(1'b0), .D(Q2), .C(Clk), .Clr(Clr), .Q(Q3));  // open: nQ
  D_FF_AS d_ff_as_5 (.Set(1'b0), .D(Q3), .C(Clk), .Clr(Clr), .Q(Q4));  // open: nQ
  D_FF_AS d_ff_as_6 (.Set(1'b0), .D(Q4), .C(Clk), .Clr(Clr), .Q(Q5));  // open: nQ
endmodule
